# Fritzing sketch Darlington_32_V5_4 (saved by Fritzing 0.9.9b)
circuit board: 16.4952cm x 4.27583cm
breadboards: 3

parts:
  MCP27017_1 = MCP23017 I2C I/O Expander
  MCP27017_2 = MCP23017 I2C I/O Expander
  MCP27017_3 = MCP23017 I2C I/O Expander
  MCP27017_4 = MCP23017 I2C I/O Expander
  5V = male pin header, 2 pins [form="♂ (male)"]
  3v3 = male pin header, 2 pins [form="♂ (male)"]
  IC1adrGND = male pin header, 3 pins [form="♂ (male)"]
  IC1adr123 = male pin header, 3 pins [form="♂ (male)"]
  IC1adr3v3 = male pin header, 3 pins [form="♂ (male)"]
  INPUT4 = male pin header, 8 pins [form="♂ (male)"]
  INPUT3 = male pin header, 8 pins [form="♂ (male)"]
  INPUT2 = male pin header, 8 pins [form="♂ (male)"]
  INPUT1 = male pin header, 8 pins [form="♂ (male)"]
  DarArr1 = IC, DIP package, 18 pins [chip_label="IC-THT Darlington"]
  DarArr2 = IC, DIP package, 18 pins [chip_label="IC-THT Darlington"]
  DarArr3 = IC, DIP package, 18 pins [chip_label="IC-THT Darlington"]
  DarArr4 = IC, DIP package, 18 pins [chip_label="IC-THT Darlington"]
  IC2adrGND = male pin header, 3 pins [form="♂ (male)"]
  IC2-ADR = male pin header, 3 pins [form="♂ (male)"]
  IC2adr3v3 = male pin header, 3 pins [form="♂ (male)"]
  IC3adr3v3 = male pin header, 3 pins [form="♂ (male)"]
  IC3-ADR = male pin header, 3 pins [form="♂ (male)"]
  IC3adrGND = male pin header, 3 pins [form="♂ (male)"]
  IC4adrGND = male pin header, 3 pins [form="♂ (male)"]
  IC4-ADR = male pin header, 3 pins [form="♂ (male)"]
  IC4adr3v3 = male pin header, 3 pins [form="♂ (male)"]
  ResArr1 = male pin header, 9 pins [form="♂ (male)"]
  ResArr2 = male pin header, 9 pins [form="♂ (male)"]
  ResArr3 = male pin header, 9 pins [form="♂ (male)"]
  ResArr4 = male pin header, 9 pins [form="♂ (male)"]
  Rly4 = male pin header, 8 pins [form="♂ (male)"]
  Rly3 = male pin header, 8 pins [form="♂ (male)"]
  Rly2 = male pin header, 8 pins [form="♂ (male)"]
  Rly1 = male pin header, 8 pins [form="♂ (male)"]
  Relay-GND-Pwr = male pin header, 2 pins [form="♂ (male)"]
  Rpi_SCL-SDA-GND_clne = double row male pin header, 6 pins [form="♂ (male)"]
  Relay-GND-Pwr1 = male pin header, 2 pins [form="♂ (male)"]

nets:
  N1: MCP27017_1.GPB0, INPUT1.pin1, ResArr1.pin9
  N2: MCP27017_1.GPB1, INPUT1.pin2, ResArr1.pin8
  N3: MCP27017_1.GPB2, INPUT1.pin3, ResArr1.pin7
  N4: MCP27017_1.GPB3, INPUT1.pin4, ResArr1.pin6
  N5: MCP27017_1.GPB4, INPUT1.pin5, ResArr1.pin5
  N6: MCP27017_1.GPB5, INPUT1.pin6, ResArr1.pin4
  N7: MCP27017_1.GPB6, INPUT1.pin7, ResArr1.pin3
  N8: MCP27017_1.GPB7, INPUT1.pin8, ResArr1.pin2
  VDD: MCP27017_1.VDD, MCP27017_2.VDD, MCP27017_3.VDD, MCP27017_4.VDD, 5V.pin1
  VSS: MCP27017_1.VSS, MCP27017_2.VSS, MCP27017_3.VSS, MCP27017_4.VSS, 5V.pin2, 3v3.pin2, IC1adrGND.pin1, IC1adr123.pin1, IC1adr3v3.pin1, DarArr1.pin9, DarArr2.pin9, DarArr3.pin9, DarArr4.pin9, IC2adrGND.pin1, IC2-ADR.pin1, IC2adr3v3.pin1, IC3adr3v3.pin1, IC3-ADR.pin1, IC3adrGND.pin1, IC4adrGND.pin1, IC4-ADR.pin1, IC4adr3v3.pin1, ResArr1.pin1, ResArr2.pin1, ResArr3.pin1, ResArr4.pin1, Relay-GND-Pwr.pin2, Rpi_SCL-SDA-GND_clne.pin1, Rpi_SCL-SDA-GND_clne.pin6, Relay-GND-Pwr1.pin2
  N9: MCP27017_1.SCL, MCP27017_2.SCL, MCP27017_3.SCL, MCP27017_4.SCL, Rpi_SCL-SDA-GND_clne.pin3, Rpi_SCL-SDA-GND_clne.pin4
  N10: MCP27017_1.SDA, MCP27017_2.SDA, MCP27017_3.SDA, MCP27017_4.SDA, Rpi_SCL-SDA-GND_clne.pin2, Rpi_SCL-SDA-GND_clne.pin5
  N11: MCP27017_1.A0, IC1adr3v3.pin2
  N12: MCP27017_1.A1, IC1adr123.pin2
  N13: MCP27017_1.A2, IC1adrGND.pin2
  N14: MCP27017_1.RESET, MCP27017_2.RESET, MCP27017_3.RESET, MCP27017_4.RESET, 3v3.pin1, IC1adrGND.pin3, IC1adr123.pin3, IC1adr3v3.pin3, IC2adrGND.pin3, IC2-ADR.pin3, IC2adr3v3.pin3, IC3adr3v3.pin3, IC3-ADR.pin3, IC3adrGND.pin3, IC4adrGND.pin3, IC4-ADR.pin3, IC4adr3v3.pin3
  N15: MCP27017_1.GPA0, DarArr1.pin8
  N16: MCP27017_1.GPA1, DarArr1.pin7
  N17: MCP27017_1.GPA2, DarArr1.pin6
  N18: MCP27017_1.GPA3, DarArr1.pin5
  N19: MCP27017_1.GPA4, DarArr1.pin4
  N20: MCP27017_1.GPA5, DarArr1.pin3
  N21: MCP27017_1.GPA6, DarArr1.pin2
  N22: MCP27017_1.GPA7, DarArr1.pin1
  N23: MCP27017_2.GPB0, INPUT2.pin1, ResArr2.pin9
  N24: MCP27017_2.GPB1, INPUT2.pin2, ResArr2.pin8
  N25: MCP27017_2.GPB2, INPUT2.pin3, ResArr2.pin7
  N26: MCP27017_2.GPB3, INPUT2.pin4, ResArr2.pin6
  N27: MCP27017_2.GPB4, INPUT2.pin5, ResArr2.pin5
  N28: MCP27017_2.GPB5, INPUT2.pin6, ResArr2.pin4
  N29: MCP27017_2.GPB6, INPUT2.pin7, ResArr2.pin3
  N30: MCP27017_2.GPB7, INPUT2.pin8, ResArr2.pin2
  N31: MCP27017_2.A0, IC2adrGND.pin2
  N32: MCP27017_2.A1, IC2-ADR.pin2
  N33: MCP27017_2.A2, IC2adr3v3.pin2
  N34: MCP27017_2.GPA0, DarArr2.pin8
  N35: MCP27017_2.GPA1, DarArr2.pin7
  N36: MCP27017_2.GPA2, DarArr2.pin6
  N37: MCP27017_2.GPA3, DarArr2.pin5
  N38: MCP27017_2.GPA4, DarArr2.pin4
  N39: MCP27017_2.GPA5, DarArr2.pin3
  N40: MCP27017_2.GPA6, DarArr2.pin2
  N41: MCP27017_2.GPA7, DarArr2.pin1
  N42: MCP27017_3.GPB0, INPUT3.pin1, ResArr3.pin9
  N43: MCP27017_3.GPB1, INPUT3.pin2, ResArr3.pin8
  N44: MCP27017_3.GPB2, INPUT3.pin3, ResArr3.pin7
  N45: MCP27017_3.GPB3, INPUT3.pin4, ResArr3.pin6
  N46: MCP27017_3.GPB4, INPUT3.pin5, ResArr3.pin5
  N47: MCP27017_3.GPB5, INPUT3.pin6, ResArr3.pin4
  N48: MCP27017_3.GPB6, INPUT3.pin7, ResArr3.pin3
  N49: MCP27017_3.GPB7, INPUT3.pin8, ResArr3.pin2
  N50: MCP27017_3.A0, IC3adr3v3.pin2
  N51: MCP27017_3.A1, IC3-ADR.pin2
  N52: MCP27017_3.A2, IC3adrGND.pin2
  N53: MCP27017_3.GPA0, DarArr3.pin8
  N54: MCP27017_3.GPA1, DarArr3.pin7
  N55: MCP27017_3.GPA2, DarArr3.pin6
  N56: MCP27017_3.GPA3, DarArr3.pin5
  N57: MCP27017_3.GPA4, DarArr3.pin4
  N58: MCP27017_3.GPA5, DarArr3.pin3
  N59: MCP27017_3.GPA6, DarArr3.pin2
  N60: MCP27017_3.GPA7, DarArr3.pin1
  N61: MCP27017_4.GPB0, INPUT4.pin1, ResArr4.pin9
  N62: MCP27017_4.GPB1, INPUT4.pin2, ResArr4.pin8
  N63: MCP27017_4.GPB2, INPUT4.pin3, ResArr4.pin7
  N64: MCP27017_4.GPB3, INPUT4.pin4, ResArr4.pin6
  N65: MCP27017_4.GPB4, INPUT4.pin5, ResArr4.pin5
  N66: MCP27017_4.GPB5, INPUT4.pin6, ResArr4.pin4
  N67: MCP27017_4.GPB6, INPUT4.pin7, ResArr4.pin3
  N68: MCP27017_4.GPB7, INPUT4.pin8, ResArr4.pin2
  N69: MCP27017_4.A0, IC4adr3v3.pin2
  N70: MCP27017_4.A1, IC4-ADR.pin2
  N71: MCP27017_4.A2, IC4adrGND.pin2
  N72: MCP27017_4.GPA0, DarArr4.pin8
  N73: MCP27017_4.GPA1, DarArr4.pin7
  N74: MCP27017_4.GPA2, DarArr4.pin6
  N75: MCP27017_4.GPA3, DarArr4.pin5
  N76: MCP27017_4.GPA4, DarArr4.pin4
  N77: MCP27017_4.GPA5, DarArr4.pin3
  N78: MCP27017_4.GPA6, DarArr4.pin2
  N79: MCP27017_4.GPA7, DarArr4.pin1
  N80: DarArr1.pin10, DarArr2.pin10, Relay-GND-Pwr.pin1
  N81: DarArr1.pin11, Rly1.pin1
  N82: DarArr1.pin12, Rly1.pin2
  N83: DarArr1.pin13, Rly1.pin3
  N84: DarArr1.pin14, Rly1.pin4
  N85: DarArr1.pin15, Rly1.pin5
  N86: DarArr1.pin16, Rly1.pin6
  N87: DarArr1.pin17, Rly1.pin7
  N88: DarArr1.pin18, Rly1.pin8
  N89: DarArr2.pin11, Rly2.pin1
  N90: DarArr2.pin12, Rly2.pin2
  N91: DarArr2.pin13, Rly2.pin3
  N92: DarArr2.pin14, Rly2.pin4
  N93: DarArr2.pin15, Rly2.pin5
  N94: DarArr2.pin16, Rly2.pin6
  N95: DarArr2.pin17, Rly2.pin7
  N96: DarArr2.pin18, Rly2.pin8
  N97: DarArr3.pin10, DarArr4.pin10, Relay-GND-Pwr1.pin1
  N98: DarArr3.pin11, Rly3.pin1
  N99: DarArr3.pin12, Rly3.pin2
  N100: DarArr3.pin13, Rly3.pin3
  N101: DarArr3.pin14, Rly3.pin4
  N102: DarArr3.pin15, Rly3.pin5
  N103: DarArr3.pin16, Rly3.pin6
  N104: DarArr3.pin17, Rly3.pin7
  N105: DarArr3.pin18, Rly3.pin8
  N106: DarArr4.pin11, Rly4.pin1
  N107: DarArr4.pin12, Rly4.pin2
  N108: DarArr4.pin13, Rly4.pin3
  N109: DarArr4.pin14, Rly4.pin4
  N110: DarArr4.pin15, Rly4.pin5
  N111: DarArr4.pin16, Rly4.pin6
  N112: DarArr4.pin17, Rly4.pin7
  N113: DarArr4.pin18, Rly4.pin8

notes:
  5V0
  3V3
  Relay board power
  MCP23017 addressing dips
  relay controls output (line J)
  Inputs (line H)
  Raspberry I2C:
  SDA (yellow) SCL (white)
  Raspberry GND
  SopelQ-D&I-64-R1

custom parts:
  MCP23017 I2C I/O Expander: The MCP23017 uses two i2c pins (these can be shared with other i2c devices), and in exchange gives you 16 general purpose pins. You can set each of 16 pins to be input, output, input with a pullup or open drain. There's even the ability to get an interrupt via an external pin when any of the inputs change so you don't have to keep polling the chip.
