# Fritzing sketch Darlington_with_INPUT_V4_1 (saved by Fritzing 0.9.9b)
circuit board: 6.3cm x 10.1cm
breadboards: 4

parts:
  MCP27017_1 = MCP23017 I2C I/O Expander
  DarArr2 = IC, DIP package, 18 pins [chip_label=IC]
  DarArr1 = IC, DIP package, 18 pins [chip_label=IC]
  MCP-AdresPINS = male pin header, 3 pins [form="♂ (male)"]
  MCP-AdresGRD = male pin header, 3 pins [form="♂ (male)"]
  RelayN1 = male pin header, 8 pins [form="♂ (male)"]
  RelayN2 = male pin header, 8 pins [form="♂ (male)"]
  5v0-GND = male pin header, 2 pins [form="♂ (male)"]
  3v3-GND = male pin header, 2 pins [form="♂ (male)"]
  Rly-GND-5v0 = male pin header, 2 pins [form="♂ (male)"]
  MCP-Adres3v3 = male pin header, 3 pins [form="♂ (male)"]
  MCP27017_2 = MCP23017 I2C I/O Expander
  MCP2-AdresPINS = male pin header, 3 pins [form="♂ (male)"]
  MCP2-Adres3v3 = male pin header, 3 pins [form="♂ (male)"]
  MCP2-AdresGRD = male pin header, 3 pins [form="♂ (male)"]
  ResArr2 = male pin header, 9 pins [form="♂ (male)"]
  ResArr1 = male pin header, 9 pins [form="♂ (male)"]
  INPUT-B = male pin header, 8 pins [form="♂ (male)"]
  INPUT-A = male pin header, 8 pins [form="♂ (male)"]
  Rpi-I2C-P3-GND-P2-SCL-P1-SDA = double row male pin header, 6 pins [form="♂ (male)"]
  RPi-MCP-IntA_IntB = male pin header, 2 pins [form="♂ (male)"]

nets:
  N1: MCP27017_1.GPB0, DarArr2.pin8
  N2: MCP27017_1.GPB1, DarArr2.pin7
  N3: MCP27017_1.GPB2, DarArr2.pin6
  N4: MCP27017_1.GPB3, DarArr2.pin5
  N5: MCP27017_1.GPB4, DarArr2.pin4
  N6: MCP27017_1.GPB5, DarArr2.pin3
  N7: MCP27017_1.GPB6, DarArr2.pin2
  N8: MCP27017_1.GPB7, DarArr2.pin1
  VDD: MCP27017_1.VDD, 5v0-GND.pin1, MCP27017_2.VDD
  VSS: MCP27017_1.VSS, DarArr2.pin9, DarArr1.pin9, MCP-AdresPINS.pin3, MCP-AdresGRD.pin3, 5v0-GND.pin2, 3v3-GND.pin2, Rly-GND-5v0.pin2, MCP-Adres3v3.pin3, MCP27017_2.VSS, MCP2-AdresPINS.pin1, MCP2-Adres3v3.pin1, MCP2-AdresGRD.pin1, ResArr2.pin1, ResArr1.pin1, Rpi-I2C-P3-GND-P2-SCL-P1-SDA.pin3, Rpi-I2C-P3-GND-P2-SCL-P1-SDA.pin4
  N9: MCP27017_1.SCL, MCP27017_2.SCL, Rpi-I2C-P3-GND-P2-SCL-P1-SDA.pin2, Rpi-I2C-P3-GND-P2-SCL-P1-SDA.pin5
  N10: MCP27017_1.SDA, MCP27017_2.SDA, Rpi-I2C-P3-GND-P2-SCL-P1-SDA.pin1, Rpi-I2C-P3-GND-P2-SCL-P1-SDA.pin6
  N11: MCP27017_1.A0, MCP-Adres3v3.pin2
  N12: MCP27017_1.A1, MCP-AdresPINS.pin2
  N13: MCP27017_1.A2, MCP-AdresGRD.pin2
  N14: MCP27017_1.RESET, MCP-AdresPINS.pin1, MCP-AdresGRD.pin1, 3v3-GND.pin1, MCP-Adres3v3.pin1, MCP27017_2.RESET, MCP2-AdresPINS.pin3, MCP2-Adres3v3.pin3, MCP2-AdresGRD.pin3
  N15: MCP27017_1.GPA0, DarArr1.pin8
  N16: MCP27017_1.GPA1, DarArr1.pin7
  N17: MCP27017_1.GPA2, DarArr1.pin6
  N18: MCP27017_1.GPA3, DarArr1.pin5
  N19: MCP27017_1.GPA4, DarArr1.pin4
  N20: MCP27017_1.GPA5, DarArr1.pin3
  N21: MCP27017_1.GPA6, DarArr1.pin2
  N22: MCP27017_1.GPA7, DarArr1.pin1
  N23: DarArr2.pin10, DarArr1.pin10, Rly-GND-5v0.pin1
  N24: DarArr2.pin11, RelayN2.pin1
  N25: DarArr2.pin12, RelayN2.pin2
  N26: DarArr2.pin13, RelayN2.pin3
  N27: DarArr2.pin14, RelayN2.pin4
  N28: DarArr2.pin15, RelayN2.pin5
  N29: DarArr2.pin16, RelayN2.pin6
  N30: DarArr2.pin17, RelayN2.pin7
  N31: DarArr2.pin18, RelayN2.pin8
  N32: DarArr1.pin11, RelayN1.pin1
  N33: DarArr1.pin12, RelayN1.pin2
  N34: DarArr1.pin13, RelayN1.pin3
  N35: DarArr1.pin14, RelayN1.pin4
  N36: DarArr1.pin15, RelayN1.pin5
  N37: DarArr1.pin16, RelayN1.pin6
  N38: DarArr1.pin17, RelayN1.pin7
  N39: DarArr1.pin18, RelayN1.pin8
  N40: MCP27017_2.GPB0, ResArr2.pin2, INPUT-B.pin8
  N41: MCP27017_2.GPB1, ResArr2.pin3, INPUT-B.pin7
  N42: MCP27017_2.GPB2, ResArr2.pin4, INPUT-B.pin6
  N43: MCP27017_2.GPB3, ResArr2.pin5, INPUT-B.pin5
  N44: MCP27017_2.GPB4, ResArr2.pin6, INPUT-B.pin4
  N45: MCP27017_2.GPB5, ResArr2.pin7, INPUT-B.pin3
  N46: MCP27017_2.GPB6, ResArr2.pin8, INPUT-B.pin2
  N47: MCP27017_2.GPB7, ResArr2.pin9, INPUT-B.pin1
  N48: MCP27017_2.A0, MCP2-Adres3v3.pin2
  N49: MCP27017_2.A1, MCP2-AdresPINS.pin2
  N50: MCP27017_2.A2, MCP2-AdresGRD.pin2
  N51: MCP27017_2.INTB, RPi-MCP-IntA_IntB.pin1
  N52: MCP27017_2.INTA, RPi-MCP-IntA_IntB.pin2
  N53: MCP27017_2.GPA0, ResArr1.pin9, INPUT-A.pin8
  N54: MCP27017_2.GPA1, ResArr1.pin8, INPUT-A.pin7
  N55: MCP27017_2.GPA2, ResArr1.pin7, INPUT-A.pin6
  N56: MCP27017_2.GPA3, ResArr1.pin6, INPUT-A.pin5
  N57: MCP27017_2.GPA4, ResArr1.pin5, INPUT-A.pin4
  N58: MCP27017_2.GPA5, ResArr1.pin4, INPUT-A.pin3
  N59: MCP27017_2.GPA6, ResArr1.pin3, INPUT-A.pin2
  N60: MCP27017_2.GPA7, ResArr1.pin2, INPUT-A.pin1

notes:
  GND
  SopelQ-D&I-32-R1

custom parts:
  MCP23017 I2C I/O Expander: The MCP23017 uses two i2c pins (these can be shared with other i2c devices), and in exchange gives you 16 general purpose pins. You can set each of 16 pins to be input, output, input with a pullup or open drain. There's even the ability to get an interrupt via an external pin when any of the inputs change so you don't have to keep polling the chip.
